# Fritzing sketch BinaryClock (saved by Fritzing 0.7.12b)
breadboards: 4

parts:
  LED1 = LED - 5mm [color="Red (633nm)" package="5 mm [THT]"]
  LED2 = LED - 5mm [color="Red (633nm)" package="5 mm [THT]"]
  LED3 = LED - 5mm [color="Red (633nm)" package="5 mm [THT]"]
  LED4 = LED - 5mm [color="Red (633nm)" package="5 mm [THT]"]
  LED5 = LED - 5mm [color="Red (633nm)" package="5 mm [THT]"]
  LED6 = LED - 5mm [color="Red (633nm)" package="5 mm [THT]"]
  LED8 = LED - 5mm [color="Red (633nm)" package="5 mm [THT]"]
  LED10 = LED - 5mm [color="Red (633nm)" package="5 mm [THT]"]
  LED7 = LED - 5mm [color="Red (633nm)" package="5 mm [THT]"]
  LED9 = LED - 5mm [color="Red (633nm)" package="5 mm [THT]"]
  LED11 = LED - 5mm [color="Red (633nm)" package="5 mm [THT]"]
  LED12 = LED - 5mm [color="Red (633nm)" package="5 mm [THT]"]
  LED13 = LED - 5mm [color="Red (633nm)" package="5 mm [THT]"]
  LED15 = LED - 5mm [color="Red (633nm)" package="5 mm [THT]"]
  LED16 = LED - 5mm [color="Red (633nm)" package="5 mm [THT]"]
  LED17 = LED - 5mm [color="Red (633nm)" package="5 mm [THT]"]
  LED14 = LED - 5mm [color="Red (633nm)" package="5 mm [THT]"]
  LED18 = LED - 5mm [color="Red (633nm)" package="5 mm [THT]"]
  R3 = Resistor [tolerance=±5% resistance=47 package=THT]
  R4 = Resistor [tolerance=±5% resistance=47 package=THT]
  R2 = Resistor [tolerance=±5% resistance=47 package=THT]
  R1 = Resistor [tolerance=±5% resistance=47 package=THT]
  R5 = Resistor [tolerance=±5% resistance=47 package=THT]
  U1 = Arduino Mega

nets:
  N1: LED1.cathode, LED2.anode, LED3.anode, LED4.cathode, LED15.anode, LED16.cathode, R2.Pin_1
  N2: LED1.anode, LED2.cathode, LED5.anode, LED6.cathode, LED13.anode, LED17.anode, LED14.cathode, LED18.cathode, R1.Pin_1
  N3: LED3.cathode, LED4.anode, LED5.cathode, LED6.anode, LED8.cathode, LED7.anode, LED11.anode, LED12.cathode, LED13.cathode, LED15.cathode, LED16.anode, LED14.anode, R3.Pin_1
  N4: LED8.anode, LED10.cathode, LED7.cathode, LED9.anode, LED17.cathode, LED18.anode, R4.Pin_1
  N5: LED10.anode, LED9.cathode, LED11.cathode, LED12.anode, R5.Pin_1
  N6: R3.Pin_0, U1.D4
  N7: R4.Pin_0, U1.D5
  N8: R2.Pin_0, U1.D3
  N9: R1.Pin_0, U1.D2
  N10: R5.Pin_0, U1.D6
